# Fritzing sketch Project2 (saved by Fritzing 0.9.2b)
breadboards: 1

parts:
  U1 = atmega328 [package=dip]
  Raspberry_Pi1 = Raspberry Pi B+  # not connected
  S1 = Round Pushbutton
  U2 = LIPO-2000mAh [package=lipo-2000]
  CAMERA1 = TTL Serial JPEG Camera  # not connected
  CHARGER1 = USB_LiIon_LiPoly_Charger_v1.2
  ANT1 = Antenna
  CONN1 = USB connector [package=THT]
  U8 = RELAY [package=relay-jzc]  # not connected
  D1 = SOLAR-IXYS [package=solarbit-12x1]
  XTAL2 = Crystal [frequency="16 Mhz" package=SMD]
  Part2 = Real Time Clock Module - DS1307 RTC Breakout Board
  Voltage_Regulator = mystery part, 4 pins [chip_label=Regulator]
  Sparkfun_Fuel_Gauge = mystery part, 8 pins [chip_label="Batt Metr"]
  BB1 = 8-Line Bi-Directional Level Shifter
  R3 = Resistor [tolerance=±5% resistance=4.7k package=THT]
  R4 = Resistor [tolerance=±5% resistance=4.7k package=THT]
  C2 = Ceramic Capacitor [capacitance=100nF package="100 mil [THT, multilayer]"]
  C3 = Ceramic Capacitor [capacitance=100nF package="100 mil [THT, multilayer]"]
  C4 = Ceramic Capacitor [capacitance=100nF package="100 mil [THT, multilayer]"]
  C5 = Ceramic Capacitor [capacitance=100nF package="100 mil [THT, multilayer]"]
  L1 = Inductor [inductance=10nH package="400 mil [THT]"]
  U9 = mystery part, 4 pins [chip_label=Bluetooth]

nets:
  N1: U1.D0_(RX), BB1.no_name_yet#2
  N2: U1.D1_(TX), BB1.no_name_yet#3, BB1.no_name_yet#4
  VCC: U1.VCC, Part2.5V, Voltage_Regulator.pin4, BB1.no_name_yet#1, R3.Pin_1, R4.Pin_1, L1.pin_1, U9.pin1
  GND: U1.GND, CHARGER1.load_minus_1, Part2.GND, Voltage_Regulator.pin3, BB1.no_name_yet#20, C2.1, C3.1, C4.0, C5.0, U9.pin2
  N3: U1.XLAT1, XTAL2.pin_0, C3.0
  N4: U1.XLAT2, XTAL2.pin_1, C2.0
  N5: U1.D8, U9.pin4
  N6: U1.D9_(PWM), U9.pin3
  N7: U1.AVCC, C5.1, L1.pin_0
  N8: U1.AREF, C4.1
  N9: U1.A4, Part2.SDA, Sparkfun_Fuel_Gauge.pin5, R3.Pin_0
  N10: U1.A5, Part2.SCL, Sparkfun_Fuel_Gauge.pin6, R4.Pin_0
  N11: S1.leg0, CHARGER1.load_plus_1
  N12: S1.leg1, Voltage_Regulator.pin1, Voltage_Regulator.pin2
  N13: U2.+, Sparkfun_Fuel_Gauge.pin1
  N14: U2.-, Sparkfun_Fuel_Gauge.pin8
  N15: CHARGER1.batt_minus_2, Sparkfun_Fuel_Gauge.pin3
  N16: CHARGER1.batt_plus_2, Sparkfun_Fuel_Gauge.pin2
  N17: CHARGER1.dcin_minus_1, D1.C
  N18: CHARGER1.dcin_plus_1, D1.A
  N19: ANT1.antenna_lead, CONN1.d+

notes:
  2500 mAh
  3.7 Volts
  Lithium Polymer
  Wifi Dongle
  Camera Module
  Latching Relay Module

custom parts:
  TTL Serial JPEG Camera: TTL Serial JPEG Camera with NTSC Out
  8-Line Bi-Directional Level Shifter: 8-channel Bi-Directional Level Shifter with TXB0108
